// Logisim project D.circ as structural Verilog: 1 circuit, main circuit main
// CP
module main (
  input  D,
  output Q,
  output Q_prime
);

  wire CP_out, NAND_2_out, NAND_out, not_1_out;

  not not_1 (not_1_out, D);
  Clock CP (.out(CP_out));
  nand NAND (NAND_out, D, CP_out);
  nand NAND_2 (NAND_2_out, CP_out, not_1_out);
  nand NAND_3 (Q, NAND_out, Q_prime);
  nand NAND_4 (Q_prime, Q, NAND_2_out);

  // Notes on the sheet:
  //   D Flip-Flop
endmodule
