// Logisim project JK.circ as structural Verilog: 1 circuit, main circuit main
module main (
  input  K,
  input  J,
  output Q,
  output Q_prime
);

  wire and_1_out, and_2_out, clock_1_out;

  Clock clock_1 (.out(clock_1_out));
  buf and_1 (and_1_out, K);  // AND_Gate
  buf and_2 (and_2_out, J);  // AND_Gate
  nor nor_1 (Q, and_1_out, Q_prime);
  nor nor_2 (Q_prime, Q, and_2_out);

  // Notes on the sheet:
  //   JK Flip-Flop
endmodule
