// Logisim project SR.circ as structural Verilog: 1 circuit, main circuit main
module main (
  input  S,
  input  R,
  output Q,
  output Q_prime
);

  wire CP_out, NAND_2_out, NAND_out;

  Clock CP (.out(CP_out));
  nand NAND (NAND_out, S, CP_out);
  nand NAND_2 (NAND_2_out, CP_out, R);
  nand NAND_3 (Q, NAND_out, Q_prime);
  nand NAND_4 (Q_prime, Q, NAND_2_out);

  // Notes on the sheet:
  //   SR Flip-Flop
endmodule
